// Logisim project Lab0 (I, II).circ as structural Verilog: 1 circuit, main circuit main
module main (
  input  A,
  input  B,
  input  C,
  input  X,
  input  Y
);

  wire _74LS04_out, _74LS08_2_out, _74LS08_3_out, _74LS08_4_out, _74LS08_out, _74LS32_2_out, _74LS32_out,
       _74LSO4_2_out, _74LSO4_out;

  not _74LSO4 (_74LSO4_out, A);
  and _74LS08 (_74LS08_out, A, C);
  not _74LS04 (_74LS04_out, X);
  not _74LSO4_2 (_74LSO4_2_out, Y);
  and _74LS08_2 (_74LS08_2_out, _74LS04_out, _74LSO4_2_out);
  and _74LS08_3 (_74LS08_3_out, _74LSO4_out, B);
  and _74LS08_4 (_74LS08_4_out, X, Y);
  or _74LS32 (_74LS32_out, _74LS08_3_out, _74LS08_out);
  or _74LS32_2 (_74LS32_2_out, _74LS08_4_out, _74LS08_2_out);
  LED f (.in(_74LS32_out));
  LED f_2 (.in(_74LS32_2_out));

  // Notes on the sheet:
  //   Part I
  //   Part II
endmodule
