// Logisim project Lab0 (III).circ as structural Verilog: 1 circuit, main circuit main
module main (
  input  a,
  input  b,
  input  c,
  input  a_2,
  input  b_2,
  input  c_2,
  input  a_3,
  input  b_3,
  input  c_3
);

  wire _74LS08_2_out, _74LS08_3_out, _74LS08_4_out, _74LS08_5_out, _74LS08_6_out, _74LS08_7_out,
       _74LS08_8_out, _74LS08_out, _74LS10_2_out, _74LS10_out, _74LS32_2_out, _74LS32_3_out, _74LS32_4_out,
       _74LS32_5_out, _74LS32_6_out, _74LS32_7_out, _74LS32_8_out, _74LS32_9_out, _74LS32_out;

  and _74LS08 (_74LS08_out, a_3, b_3);
  and _74LS08_2 (_74LS08_2_out, b_3, c_3);
  and _74LS08_3 (_74LS08_3_out, a, b);
  and _74LS08_4 (_74LS08_4_out, b, c);
  and _74LS08_5 (_74LS08_5_out, a, c);
  buf _74LS32 (_74LS32_out, a_2);  // OR_Gate
  or _74LS32_2 (_74LS32_2_out, b_2, c_2);
  or _74LS32_3 (_74LS32_3_out, _74LS32_out, _74LS32_2_out);
  and _74LS08_6 (_74LS08_6_out, a_3, c_3);
  nand _74LS10 (_74LS10_out, c_2, b_2, a_2);
  or _74LS32_4 (_74LS32_4_out, _74LS08_4_out, _74LS08_5_out);
  and _74LS08_7 (_74LS08_7_out, _74LS32_3_out, _74LS10_out);
  buf _74LS32_5 (_74LS32_5_out, _74LS08_out);  // OR_Gate
  or _74LS32_6 (_74LS32_6_out, _74LS08_2_out, _74LS08_6_out);
  nand _74LS10_2 (_74LS10_2_out, c_3, b_3, a_3);
  or _74LS32_7 (_74LS32_7_out, _74LS08_3_out, _74LS08_3_out);
  or _74LS32_8 (_74LS32_8_out, _74LS32_5_out, _74LS32_6_out);
  LED f1 (.in(_74LS32_9_out));
  or _74LS32_9 (_74LS32_9_out, _74LS32_7_out, _74LS32_4_out);
  LED f2 (.in(_74LS08_7_out));
  and _74LS08_8 (_74LS08_8_out, _74LS32_8_out, _74LS10_2_out);
  LED f3 (.in(_74LS08_8_out));

  // Notes on the sheet:
  //   a)
  //   b)
  //   c)
  //   Part III
endmodule
